# Fritzing sketch electronics-final (saved by Fritzing 0.9.3b)
breadboards: 1

parts:
  Raspberry_Pi_Zero1 = Raspberry Pi Zero
  Q2 = NPN-Transistor [package="SOT-23 [SMD]"]
  LED2 = LED - 3mm [color="Infrared (940nm)" package="3 mm [THT]"]
  LED1 = LED - 5mm [color="White (6500K)" package="5 mm [THT]"]
  R5 = Resistor [tolerance=±5% resistance=10k package=THT]
  R6 = Resistor [tolerance=±5% resistance=4.7k package=THT]
  R7 = Resistor [tolerance=±5% resistance=100 package=THT]
  R8 = Resistor [tolerance=±5% resistance=100 package=THT]
  S1 = Round Pushbutton
  S2 = Round Pushbutton
  S3 = Round Pushbutton
  U1 = QRD1114 [package=qrd1114]

nets:
  N1: Raspberry_Pi_Zero1.3v3, R7.Pin_1, U1.A, U1.K
  N2: Raspberry_Pi_Zero1.GND, Q2.2, LED1.cathode, R6.Pin_1, R8.Pin_1, S1.leg0, S2.leg0, S3.leg0
  N3: Raspberry_Pi_Zero1.GPIO17, R6.Pin_0, U1.C
  N4: Raspberry_Pi_Zero1.GPIO27, LED1.anode
  N5: Raspberry_Pi_Zero1.GPIO22, R5.Pin_1
  N6: Raspberry_Pi_Zero1.GPIO10, S1.leg1
  N7: Raspberry_Pi_Zero1.GPIO9, S2.leg1
  N8: Raspberry_Pi_Zero1.GPIO11, S3.leg1
  N9: Q2.0, R5.Pin_0
  N10: Q2.1, LED2.cathode
  N11: LED2.anode, R7.Pin_0
  N12: R8.Pin_0, U1.E

notes:
  GPIO 18, 19 and 21 along with PIN 4 and 6 (5V and GND) are used by the PHAT DAC. (Marked with orange cables.)

custom parts:
  QRD1114: Reflective object sensor
